# Fritzing sketch MyoUnoHand (saved by Fritzing 0.9.2b)
breadboards: 1

parts:
  Part1 = Arduino Uno (Rev3)
  U1 = BLUETOOTH-RN41 [package=rn41]
  R1 = Resistor [tolerance=±5% resistance=220 package=THT]
  R2 = Basic Flex Resistor
  R3 = Resistor [tolerance=±5% resistance=220 package="2010 [SMD]"]
  R4 = Basic Flex Resistor
  R5 = Basic Flex Resistor
  R6 = Resistor [tolerance=±5% resistance=220 package="2010 [SMD]"]
  R7 = Resistor [tolerance=±5% resistance=220 package="2010 [SMD]"]
  R8 = Resistor [tolerance=±5% resistance=220 package="0402 [SMD]"]
  R9 = Basic Flex Resistor
  R10 = Resistor [tolerance=±5% resistance=220 package="2010 [SMD]"]
  R12 = Basic Flex Resistor
  R13 = Resistor [tolerance=±5% resistance=220 package="2010 [SMD]"]

nets:
  N1: Part1.A0, R2.Pin_2, R3.Pin_0
  N2: Part1.A1, R4.Pin_2, R6.Pin_0
  N3: Part1.A2, R5.Pin_2, R7.Pin_0
  N4: Part1.A3, R9.Pin_2, R10.Pin_0
  N5: Part1.A4/SDA, R12.Pin_2, R13.Pin_0
  N6: Part1.GND, U1.USBD+, R3.Pin_1, R6.Pin_1, R7.Pin_1, R8.Pin_1, R10.Pin_1, R13.Pin_1
  N7: Part1.D0/RX, U1.PIO2
  N8: Part1.D1/TX, R1.Pin_0
  N9: Part1.5V, U1.PIO3, R2.pin_1, R4.pin_1, R5.pin_1, R9.pin_1, R12.pin_1
  N10: U1.USBD-, R1.Pin_1

notes:
  This is not the bluetooth peripheral we used, just here for representation (HC-06 was used)
  For hooking up wifi, 2200 ohm for actually circuit, ~1k ohm for grounding
  For each flex sensor, 2200 ohm resistor in split circuit, normalizing 30-180 integer response to be between 0-90 (reversed)
